# Fritzing sketch GarbageReminder (saved by Fritzing 0.9.3b)

parts:
  Pro_Micro = Arduino Pro Mini (3.3V)
  RTC_ZS042 = ZS-042 RTC Module
  OLED_128x64 = OLED 128x64 I2C Monochrome Display
  S1 = Pushbutton [package="[SMD]"]
  LED1 = LEDs [package=led10mm]
  R1 = Resistor [tolerance=±5% resistance=150 package="0402 [SMD]"]

nets:
  GND: Pro_Micro.GND, RTC_ZS042.GND, OLED_128x64.GND, S1.Pin_3, S1.Pin_4, R1.Pin_1
  VCC: Pro_Micro.VCC, RTC_ZS042.VCC, OLED_128x64.VDD
  N1: Pro_Micro.D10, LED1.C
  N2: Pro_Micro.D7, S1.Pin_1, S1.Pin_2
  N3: Pro_Micro.D3, RTC_ZS042.SCL, OLED_128x64.SCK
  N4: Pro_Micro.D2, RTC_ZS042.SDA, OLED_128x64.SDA
